// Logisim project project_1.circ as structural Verilog: 1 circuit, main circuit main
module main (
);

  wire and_1_out, button_1_out, clock_1_out, comparator_1_lt, comparator_2_gt, multiplexer_1_out, nor_1_out;
  wire [1:0] adder_2_out, bit_extender_2_out, bit_extender_3_out, shifter_1_out;
  wire [7:0] adder_1_out, adder_3_out, bit_extender_1_out, multiplexer_2_out, multiplexer_3_out,
       multiplexer_4_out, multiplexer_5_out, negator_1_out, register_1_q, register_2_q, rom_1_data,
       subtractor_1_out;

  Clock clock_1 (.out(clock_1_out));
  Adder adder_1 (.a(8'h1), .b(register_1_q), .out(adder_1_out));  // open: cin, cout
  Register register_1 (.D(adder_1_out), .clk(clock_1_out), .Q(register_1_q), .clr(button_1_out));  // open: en
  Button button_1 (.out(button_1_out));
  ROM rom_1 (.addr(register_1_q), .data(rom_1_data));
  nor nor_1 (nor_1_out, rom_1_data[7], rom_1_data[6]);
  and and_1 (and_1_out, rom_1_data[7], rom_1_data[6]);
  assign bit_extender_1_out = {{2{1'b0}}, rom_1_data[5:0]};  // Bit_Extender bit_extender_1
  Multiplexer multiplexer_1 (.in0(rom_1_data[6]), .in1(rom_1_data[5]), .out(multiplexer_1_out), .sel(and_1_out));
  Register register_2 (.D(multiplexer_5_out), .en(1'b1), .clk(clock_1_out), .Q(register_2_q), .clr(button_1_out));
  assign bit_extender_2_out = {{1{1'b0}}, multiplexer_1_out};  // Bit_Extender bit_extender_2
  assign bit_extender_3_out = {{1{1'b0}}, and_1_out};  // Bit_Extender bit_extender_3
  Shifter #(.width(2)) shifter_1 (.in(bit_extender_3_out), .\dist (1'b1), .out(shifter_1_out));
  Multiplexer #(.width(8)) multiplexer_2 (
    .in0(register_2_q), .in1({8{1'b0}}), .out(multiplexer_2_out), .sel(nor_1_out));
  Negator negator_1 (.in(multiplexer_2_out), .out(negator_1_out));
  Adder #(.width(2)) adder_2 (.a(bit_extender_2_out), .b(shifter_1_out), .out(adder_2_out));  // open: cin, cout
  Adder adder_3 (.a(bit_extender_1_out), .b(multiplexer_2_out), .out(adder_3_out));  // open: cin, cout
  Subtractor subtractor_1 (.a(multiplexer_2_out), .b(bit_extender_1_out), .out(subtractor_1_out));  // open: bin, bout
  Multiplexer #(.width(8)) multiplexer_3 (
    .in0({8{1'b0}}), .in1(multiplexer_2_out), .out(multiplexer_3_out), .sel(comparator_1_lt));
  Comparator comparator_1 (.a({8{1'b0}}), .b(multiplexer_2_out), .lt(comparator_1_lt));  // open: gt, eq
  Multiplexer #(.width(8)) multiplexer_4 (
    .in0(negator_1_out), .in1(multiplexer_2_out), .out(multiplexer_4_out), .sel(comparator_2_gt));
  Comparator comparator_2 (.a(negator_1_out), .b(multiplexer_2_out), .gt(comparator_2_gt));  // open: eq, lt
  Multiplexer #(.select(2), .width(8)) multiplexer_5 (
    .in0(adder_3_out), .in1(subtractor_1_out), .in2(multiplexer_3_out), .in3(multiplexer_4_out),
    .out(multiplexer_5_out), .sel(adder_2_out));

  // Notes on the sheet:
  //   reset program
  //   contents of rom_1 (hex, n*v repeats v):
  //   21 82 5e e0 c0
  //   imediato
  //   Relu
  //   Abs
  //   imm
  //   reg
  //   reg
  //   imm
  //   Addi
  //   Subi
  //   bit seletor
  //   output
endmodule
